// Digital circuit D flip-flop.dig as structural Verilog
module D_flip_flop (
  input  D,
  input  CLK,
  output Q,
  output NOT_Q
);

  wire d_latch_1_p2;

  // D_latch d_latch_1: pin names not known; wires that end beside it: D, d_latch_1_p2
  // Not not_1 has open pins: in=CLK, out=open
  // D_latch d_latch_2: pin names not known; wires that end beside it: d_latch_1_p2, CLK, Q, NOT_Q
endmodule
